// Logisim project Yerassyl_Myrzakhanov_Week2Lab.circ as structural Verilog: 1 circuit, main circuit main
module main (
  input  in_1,
  input  IN1,
  input  IN2,
  output OUT1
);

  wire and_1_out, and_2_out, not_1_out, not_2_out;

  not not_1 (not_1_out, in_1);
  not not_2 (not_2_out, not_1_out);
  and and_1 (and_1_out, not_2_out, IN1);
  and and_2 (and_2_out, not_1_out, IN2);
  or or_1 (OUT1, and_1_out, and_2_out);

  // Notes on the sheet:
  //   SEL
endmodule
